# Fritzing sketch Projet patate (saved by Fritzing 0.9.2b)
breadboards: 1

parts:
  R2 = Resistor [tolerance=±5% resistance=220 package="2512 [SMD]"]
  Composant1 = Arduino Uno (Rev3) - ICSP
  LED1 = smd LED [color="Red (633nm)" package="1206 [SMD]"]  # not connected
  LED2 = RGB LED (com. cathode, rbg) [package="5 mm [THT]"]
  R3 = Resistor [tolerance=±5% resistance=220 package="2512 [SMD]"]
  R4 = Resistor [tolerance=±5% resistance=220 package="2512 [SMD]"]
  C1 = Electrolytic Capacitor [capacitance=1000μF package="1010 [SMD, electrolytic]"]
  R5 = Resistor [tolerance=±5% resistance=10k package="0603 [SMD]"]
  R6 = Resistor [tolerance=±5% resistance=3.3k package="0603 [SMD]"]
  D1 = Rectifier Diode [package="Melf DO-213 AA [SMD]"]
  R7 = Resistor [tolerance=±5% resistance=1M package="0603 [SMD]"]
  C2 = Electrolytic Capacitor [capacitance=0.1mF package="1010 [SMD, electrolytic]"]
  L3 = Inductor [inductance=10mH package="400 mil [THT]"]

nets:
  N1: R2.Pin_0, LED2.green_anode
  N2: R2.Pin_1, Composant1.ICSP_MISO, Composant1.D12/MISO
  N3: Composant1.A0, D1.cathode, R7.Pin_1, C2.+
  N4: Composant1.ICSP_MOSI, Composant1.D11_PWM/MOSI, R3.Pin_1
  N5: Composant1.D9_PWM, R5.Pin_1
  N6: Composant1.D10_PWM/SS, R4.Pin_1
  N7: Composant1.GND, LED2.red_anode, R6.Pin_0, R7.Pin_0, C2.-
  N8: LED2.common_cathode, R4.Pin_0
  N9: LED2.blue_anode, R3.Pin_0
  N10: C1.+, D1.anode, L3.pin_0
  N11: R5.Pin_0, R6.Pin_1, L3.pin_1
